# Fritzing sketch feather-knob-button (saved by Fritzing 0.9.3b)
breadboards: 1

parts:
  Part1 = Adafruit Feather M0 Express [part_number="Adafruit #3403"]
  R1 = Rotary Potentiometer (Small) [maximum_resistance=100kΩ package=THT]
  S1 = Pushbutton [package="[THT]"]

nets:
  N1: Part1.GND, R1.leg2
  N2: Part1.A2, R1.wiper
  N3: Part1.+3V3, R1.leg1
  N4: Part1.D10, S1.Pin_3, S1.Pin_4
  N5: S1.Pin_1, S1.Pin_2

custom parts:
  Adafruit Feather M0 Express: We love all our Feathers equally, but this Feather is very special. It's our first Feather that is specifically designed for use with CircuitPython! CircuitPython is our beginner-oriented flavor of MicroPython - and as the name hints at, its a small but full-featured version of the popular Python programming language specifically for use with circuitry and electronics. That doesn't mean you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
